# Fritzing sketch OkulProje (saved by Fritzing 0.8.7b)
breadboards: 1

parts:
  U1 = ESP8266 NodeMCU LoLin module
  U2 = GAS_SENSOR [package=mq-3]
  LED1 = LED - 5mm [color="Red (633nm)" package="5 mm [THT]"]
  R1 = Resistor [tolerance=±5% resistance=220 package=THT]

nets:
  N1: U1.3V3, U2.B1
  N2: U1.GND, LED1.cathode
  N3: U1.A0, U2.A1
  N4: LED1.anode, R1.Pin_0

notes:
  MQ2 Gaz ve Duman Sensörü

custom parts:
  ESP8266 NodeMCU LoLin module: ESP8266 based NodeMCU
